# Fritzing sketch fritzing_setup (saved by Fritzing 0.9.2b)
breadboards: 1

parts:
  Part1 = Arduino Uno (Rev3) - ICSP
  Part2 = MPR121 Breakout
  Part3 = MPR121 Breakout

nets:
  3.3V: Part1.3V3, Part2.3.3V, Part3.3.3V
  GND: Part1.GND, Part2.GND, Part3.GND
